// Logisim project 2019202103_이은비_Project_0.circ.circ as structural Verilog: 2 circuits, main circuit main
module main (
  input  RST,
  input  in_2
);

  wire and_1_out, and_2_out, and_3_out, and_4_out, and_5_out, CLK_out, comparator_1_eq, comparator_1_gt,
       control_1_irce, d_ff_1_q, decoder_1_out0, decoder_1_out1, decoder_1_out2, decoder_1_out3,
       decoder_1_out4, decoder_1_out5, decoder_1_out6, decoder_1_out7, decoder_1_out8, decoder_1_out9,
       decoder_1_out10, decoder_1_out11, decoder_1_out12, decoder_1_out13, decoder_1_out14, decoder_1_out15,
       multiplexer_3_out, nor_1_out, not_1_out, not_2_out, not_3_out, not_5_out, or_1_out, or_2_out,
       or_3_out, or_4_out, w1, w2, w3, w4, w5, w6, w7, w8;
  wire [1:0] control_1_alufs;
  wire [3:0] ACC_q, ACC_q_2, ACC_q_3, ACC_q_4, bit_extender_1_out, multiplexer_2_out, multiplexer_2_out_2,
       multiplexer_2_out_3, opcode, PC_q, PC_q_2, PC_q_3;
  wire [11:0] adder_1_out, IR_q, multiplexer_1_out;
  wire [15:0] adder_2_out, multiplexer_4_out, multiplexer_5_out, not_4_out, ram_1_dout;

  Clock CLK (.out(CLK_out));
  not not_1 (not_1_out, d_ff_1_q);
  D_Flip_Flop d_ff_1 (.D(not_1_out), .clk(CLK_out), .Q(d_ff_1_q), .reset(RST));  // open: Qn, preset
  Hex_Digit_Display hex_digit_display_1 (.value(PC_q_3));  // open: dp
  or or_1 (or_1_out, and_5_out, and_4_out);
  Adder #(.width(12)) adder_1 (
    .a({PC_q_3, PC_q_2, PC_q}), .b({12{1'b0}}), .out(adder_1_out), .cin(1'b1));  // open: cout
  or or_2 (or_2_out, and_4_out, d_ff_1_q);
  not not_2 (not_2_out, d_ff_1_q);
  Hex_Digit_Display hex_digit_display_2 (.value(PC_q_2));  // open: dp
  Hex_Digit_Display hex_digit_display_3 (.value(PC_q));  // open: dp
  Register #(.width(12)) PC (
    .D(multiplexer_1_out), .en(and_1_out), .clk(CLK_out), .Q({PC_q_3, PC_q_2, PC_q}), .clr(RST));
  Multiplexer #(.width(12)) multiplexer_1 (.in0(adder_1_out), .in1(IR_q), .out(multiplexer_1_out));  // open: sel
  and and_1 (and_1_out, or_2_out, w7);
  control control_1 (
    .opcode(opcode), .reset(in_2), .Asel(w6), .Bsel(w4), .ACCce(w3), .PCce(w7), .IRce(control_1_irce),
    .ACCoe(w1), .ALUfs(control_1_alufs), .MEMrq(w8), .RnW(w5), .out_15(w2));  // open: ExnFt, ACCz, ACC15
  Hex_Digit_Display hex_digit_display_4 (.value(multiplexer_2_out_3));  // open: dp
  Multiplexer #(.width(12)) multiplexer_2 (
    .in0({PC_q_3, PC_q_2, PC_q}), .in1(IR_q),
    .out({multiplexer_2_out_3, multiplexer_2_out_2, multiplexer_2_out}), .sel(d_ff_1_q));
  not not_3 (not_3_out, CLK_out);
  Hex_Digit_Display hex_digit_display_5 (.value(multiplexer_2_out_2));  // open: dp
  Hex_Digit_Display hex_digit_display_6 (.value(multiplexer_2_out));  // open: dp
  and and_2 (and_2_out, w8, d_ff_1_q);
  Multiplexer multiplexer_3 (.in0(1'b0), .in1(1'b1), .out(multiplexer_3_out), .sel(w2));
  RAM #(.addrWidth(12), .asyncread("true"), .dataWidth(16)) ram_1 (
    .addr({multiplexer_2_out_3, multiplexer_2_out_2, multiplexer_2_out}), .we(and_2_out), .oe(1'b1),
    .clk(CLK_out), .din({ACC_q_4, ACC_q_3, ACC_q_2, ACC_q}), .dout(ram_1_dout));
  Multiplexer #(.width(16)) multiplexer_4 (
    .in0({ACC_q_4, ACC_q_3, ACC_q_2, ACC_q}), .in1({16{1'b0}}), .out(multiplexer_4_out));  // open: sel
  Multiplexer #(.width(16)) multiplexer_5 (.in0(ram_1_dout), .in1(not_4_out), .out(multiplexer_5_out));  // open: sel
  assign not_4_out = ~ram_1_dout;  // NOT_Gate not_4, 16 bits wide
  // Probe on nothing
  // Probe on ram_1_dout
  Adder #(.width(16)) adder_2 (
    .a(multiplexer_4_out), .b(multiplexer_5_out), .out(adder_2_out), .cin(multiplexer_3_out));  // open: cout
  // Probe on nothing
  or or_3 (or_3_out, w1, w3);
  // Probe on nothing
  Register #(.width(16)) ACC (
    .D(adder_2_out), .en(and_3_out), .clk(CLK_out), .Q({ACC_q_4, ACC_q_3, ACC_q_2, ACC_q}), .clr(RST));
  and and_3 (and_3_out, or_3_out, d_ff_1_q);
  Register #(.width(16)) IR (.D(ram_1_dout), .en(not_2_out), .clk(CLK_out), .Q({opcode, IR_q}), .clr(RST));
  // Probe on IR_q
  assign bit_extender_1_out = {{3{1'b0}}, d_ff_1_q};  // Bit_Extender bit_extender_1
  Comparator #(.width(16)) comparator_1 (
    .a({ACC_q_4, ACC_q_3, ACC_q_2, ACC_q}), .b({16{1'b0}}), .gt(comparator_1_gt), .eq(comparator_1_eq));  // open: lt
  Hex_Digit_Display hex_digit_display_7 (.value(ACC_q_4));  // open: dp
  Hex_Digit_Display hex_digit_display_8 (.value(opcode));  // open: dp
  Hex_Digit_Display hex_digit_display_9 (.value(bit_extender_1_out));  // open: dp
  Hex_Digit_Display hex_digit_display_10 (.value(ACC_q_3));  // open: dp
  Hex_Digit_Display hex_digit_display_11 (.value(ACC_q_2));  // open: dp
  or or_4 (or_4_out, comparator_1_gt, comparator_1_eq);
  not not_5 (not_5_out, comparator_1_eq);
  Hex_Digit_Display hex_digit_display_12 (.value(ACC_q));  // open: dp
  Decoder #(.enable("false"), .select(4)) decoder_1 (
    .out0(decoder_1_out0), .out1(decoder_1_out1), .out2(decoder_1_out2), .out3(decoder_1_out3),
    .out4(decoder_1_out4), .out5(decoder_1_out5), .out6(decoder_1_out6), .out7(decoder_1_out7),
    .out8(decoder_1_out8), .out9(decoder_1_out9), .out10(decoder_1_out10), .out11(decoder_1_out11),
    .out12(decoder_1_out12), .out13(decoder_1_out13), .out14(decoder_1_out14), .out15(decoder_1_out15),
    .sel(opcode));
  nor nor_1 (nor_1_out, decoder_1_out7, decoder_1_out8, decoder_1_out9, decoder_1_out10, decoder_1_out11, decoder_1_out12, decoder_1_out13, decoder_1_out14, decoder_1_out15);
  and and_4 (and_4_out, or_4_out, w4);
  and and_5 (and_5_out, not_5_out, w5);

  // Notes on the sheet:
  //                                    program counter
  //                                 Memory Address
  //           Opcode
  //   Machine State
  //   Accumulator Value
endmodule

module control (
  input  [3:0] opcode,
  input  reset,
  input  ExnFt,
  input  ACCz,
  input  ACC15,
  output Asel,
  output Bsel,
  output ACCce,
  output PCce,
  output IRce,
  output ACCoe,
  output [1:0] ALUfs,
  output MEMrq,
  output RnW,
  output out_15
);

  wire and_1_out, and_2_out, and_3_out, and_4_out, and_5_out, and_7_out, and_8_out, and_9_out, and_10_out,
       and_11_out, and_12_out, and_13_out, and_14_out, and_15_out, and_16_out, and_18_out, and_19_out,
       and_20_out, and_21_out, not_1_out, not_2_out, not_3_out, not_4_out, not_5_out, not_6_out, not_7_out;

  not not_1 (not_1_out, opcode[2]);
  not not_2 (not_2_out, opcode[1]);
  not not_3 (not_3_out, opcode[0]);
  not not_4 (not_4_out, reset);
  not not_5 (not_5_out, ExnFt);
  not not_6 (not_6_out, ACCz);
  not not_7 (not_7_out, ACC15);
  and and_1 (and_1_out, not_1_out, not_4_out, not_5_out);
  and and_2 (and_2_out, opcode[2], not_2_out, not_3_out, not_4_out);
  and and_3 (and_3_out, opcode[2], opcode[0], not_4_out, not_7_out);
  and and_4 (and_4_out, opcode[2], opcode[1], not_4_out, not_6_out);
  and and_5 (and_5_out, opcode[2], opcode[1], opcode[0], not_4_out);
  and and_6 (Bsel, not_1_out, not_4_out, not_5_out);
  and and_7 (and_7_out, not_1_out, not_3_out, not_5_out);
  and and_8 (and_8_out, not_1_out, opcode[1], not_5_out);
  and and_9 (and_9_out, not_1_out, ExnFt);
  and and_10 (and_10_out, not_3_out, ExnFt);
  and and_11 (and_11_out, opcode[2], not_2_out);
  and and_12 (and_12_out, opcode[2], not_3_out);
  and and_13 (and_13_out, not_1_out, ExnFt);
  and and_14 (and_14_out, not_3_out, ExnFt);
  and and_15 (and_15_out, opcode[2], not_2_out);
  and and_16 (and_16_out, opcode[2], not_3_out);
  and and_17 (ACCoe, not_1_out, not_2_out, opcode[0], not_4_out, not_5_out);
  and and_18 (and_18_out, not_1_out, opcode[1]);
  and and_19 (and_19_out, opcode[2], not_2_out, not_3_out);
  and and_20 (and_20_out, opcode[2], opcode[0]);
  and and_21 (and_21_out, opcode[2], opcode[1]);
  or or_1 (MEMrq, not_1_out, not_2_out, not_3_out, reset);
  or or_2 (RnW, not_3_out, ExnFt, reset, opcode[1], opcode[2]);
  and and_22 (out_15, not_1_out, not_4_out, not_5_out);
  or or_3 (Asel, and_1_out, and_2_out, and_3_out, and_4_out, and_5_out);
  or or_4 (ACCce, and_7_out, reset, and_8_out);
  or or_5 (PCce, and_9_out, and_10_out, reset, and_11_out, and_12_out);
  or or_6 (IRce, and_13_out, and_14_out, reset, and_15_out, and_16_out);
  or or_7 (ALUfs[1], and_18_out, and_19_out);
  or or_8 (ALUfs[0], and_20_out, and_21_out);
endmodule
